// Logisim project 16bitCPU.circ as structural Verilog: 12 circuits, main circuit main
module main (
);

  wire CLK, clock_1_out, cpu_1_halt, decimaldisplaycontrol_1_sign, frontpanelcontroller_1_runhalt, Reset,
       RunStop_out, Step_out;
  wire [3:0] cpu_1_aluflags, cpu_1_flags, decimaldisplaycontrol_1_d0, decimaldisplaycontrol_1_d1,
       decimaldisplaycontrol_1_d2, decimaldisplaycontrol_1_d3, decimaldisplaycontrol_1_d4;
  wire [15:0] cpu_1_alua, cpu_1_alub, cpu_1_aluresult, cpu_1_imaddress, cpu_1_imdata, cpu_1_writeback,
       decimalio_1_data, DMAddress, DMDataIn, IM_data;

  Clock clock_1 (.out(clock_1_out));
  ROM #(.addrWidth(16), .dataWidth(16)) IM (.addr(cpu_1_imaddress), .data(IM_data));
  FrontPanelController frontpanelcontroller_1 (
    .Clk(clock_1_out), .Run(RunStop_out), .Step(Step_out), .Reset(Reset), .Halt(cpu_1_halt), .CpuClk(CLK),
    .RunHalt(frontpanelcontroller_1_runhalt));
  CPU cpu_1 (
    .CLK(CLK), .Reset(Reset), .IMDataIn(IM_data), .Halt(cpu_1_halt), .IMAddress(cpu_1_imaddress),
    .IMData(cpu_1_imdata), .DMAddress(DMAddress), .DMData(DMDataIn), .WriteBack(cpu_1_writeback),
    .Flags(cpu_1_flags), .AluA(cpu_1_alua), .AluB(cpu_1_alub), .ALUResult(cpu_1_aluresult),
    .ALUFlags(cpu_1_aluflags));
  LED led_1 (.in(cpu_1_flags[3]));
  LED led_2 (.in(cpu_1_flags[2]));
  LED led_3 (.in(cpu_1_flags[1]));
  LED led_4 (.in(cpu_1_flags[0]));
  Hex_Digit_Display hex_digit_display_1 (.value(cpu_1_alua[15:12]));  // open: dp
  LED led_5 (.in(cpu_1_halt));
  Hex_Digit_Display hex_digit_display_2 (.value(cpu_1_imaddress[15:12]));  // open: dp
  Hex_Digit_Display hex_digit_display_3 (.value(cpu_1_imaddress[11:8]));  // open: dp
  Hex_Digit_Display hex_digit_display_4 (.value(cpu_1_imdata[15:12]));  // open: dp
  Hex_Digit_Display hex_digit_display_5 (.value(cpu_1_imdata[11:8]));  // open: dp
  Hex_Digit_Display hex_digit_display_6 (.value(cpu_1_alua[11:8]));  // open: dp
  Hex_Digit_Display hex_digit_display_7 (.value(cpu_1_alua[7:4]));  // open: dp
  LED N (.in(cpu_1_aluflags[3]));
  LED Z (.in(cpu_1_aluflags[2]));
  LED C (.in(cpu_1_aluflags[1]));
  LED led_6 (.in(frontpanelcontroller_1_runhalt));
  Button RunStop (.out(RunStop_out));
  Hex_Digit_Display hex_digit_display_8 (.value(cpu_1_imaddress[7:4]));  // open: dp
  Hex_Digit_Display hex_digit_display_9 (.value(cpu_1_imaddress[3:0]));  // open: dp
  Hex_Digit_Display hex_digit_display_10 (.value(cpu_1_imdata[7:4]));  // open: dp
  // Hex_Digit_Display hex_digit_display_11: pin names not known; wires that end beside it: cpu_1_imdata[3:0]
  Hex_Digit_Display hex_digit_display_12 (.value(cpu_1_alua[3:0]));  // open: dp
  LED V (.in(cpu_1_aluflags[0]));
  Button Step (.out(Step_out));
  Hex_Digit_Display hex_digit_display_13 (.value(DMAddress[15:12]));  // open: dp
  Hex_Digit_Display hex_digit_display_14 (.value(DMDataIn[15:12]));  // open: dp
  Hex_Digit_Display hex_digit_display_15 (.value(cpu_1_writeback[15:12]));  // open: dp
  Hex_Digit_Display hex_digit_display_16 (.value(cpu_1_alub[15:12]));  // open: dp
  Hex_Digit_Display hex_digit_display_17 (.value(cpu_1_aluresult[15:12]));  // open: dp
  Button u_Reset (.out(Reset));
  Hex_Digit_Display hex_digit_display_18 (.value(DMAddress[11:8]));  // open: dp
  Hex_Digit_Display hex_digit_display_19 (.value(DMAddress[7:4]));  // open: dp
  Hex_Digit_Display hex_digit_display_20 (.value(DMDataIn[11:8]));  // open: dp
  Hex_Digit_Display hex_digit_display_21 (.value(DMDataIn[7:4]));  // open: dp
  Hex_Digit_Display hex_digit_display_22 (.value(cpu_1_writeback[11:8]));  // open: dp
  Hex_Digit_Display hex_digit_display_23 (.value(cpu_1_writeback[7:4]));  // open: dp
  Hex_Digit_Display hex_digit_display_24 (.value(cpu_1_alub[11:8]));  // open: dp
  Hex_Digit_Display hex_digit_display_25 (.value(cpu_1_alub[7:4]));  // open: dp
  Hex_Digit_Display hex_digit_display_26 (.value(cpu_1_aluresult[11:8]));  // open: dp
  Hex_Digit_Display hex_digit_display_27 (.value(cpu_1_aluresult[7:4]));  // open: dp
  _7_Segment_Display u_7_segment_display_1 (.g(decimaldisplaycontrol_1_sign));  // open: f, a, b, e, d, c, dp
  Hex_Digit_Display hex_digit_display_28 (.value(DMAddress[3:0]));  // open: dp
  Hex_Digit_Display hex_digit_display_29 (.value(DMDataIn[3:0]));  // open: dp
  Hex_Digit_Display hex_digit_display_30 (.value(cpu_1_writeback[3:0]));  // open: dp
  Hex_Digit_Display hex_digit_display_31 (.value(cpu_1_alub[3:0]));  // open: dp
  Hex_Digit_Display hex_digit_display_32 (.value(cpu_1_aluresult[3:0]));  // open: dp
  Hex_Digit_Display hex_digit_display_33 (.value(decimaldisplaycontrol_1_d3));  // open: dp
  Hex_Digit_Display hex_digit_display_34 (.value(decimaldisplaycontrol_1_d4));  // open: dp
  Hex_Digit_Display hex_digit_display_35 (.value(decimaldisplaycontrol_1_d2));  // open: dp
  Hex_Digit_Display hex_digit_display_36 (.value(decimaldisplaycontrol_1_d1));  // open: dp
  Hex_Digit_Display hex_digit_display_37 (.value(decimaldisplaycontrol_1_d0));  // open: dp
  DecimalDisplayControl decimaldisplaycontrol_1 (
    .DataIn(decimalio_1_data), .D0(decimaldisplaycontrol_1_d0), .D1(decimaldisplaycontrol_1_d1),
    .D2(decimaldisplaycontrol_1_d2), .D3(decimaldisplaycontrol_1_d3), .D4(decimaldisplaycontrol_1_d4),
    .Sign(decimaldisplaycontrol_1_sign));
  DecimalIO decimalio_1 (.DMData(DMDataIn), .DMAddress(DMAddress), .CLK(CLK), .RESET(Reset), .Data(decimalio_1_data));

  // Notes on the sheet:
  //   contents of IM (hex, n*v repeats v):
  //   8000 9080 1031 8000 9001 c000 d001 b000 0 b000 1903 858 2009 8c0 2125 239c 7ff8 600
  //   N  Z  C  V
  //   Latched Flags
  //   HALT
  //   Instruction Memory
  //   mARMi
  //   ALU A Input
  //   ALU Flags
  //   Data Memory
  //   WriteBack
  //   ALU B Input
  //   ALU Result
endmodule

module CPU (
  input  CLK,
  input  Reset,
  input  [15:0] IMDataIn,
  output Halt,
  output [15:0] IMAddress,
  output [15:0] IMData,
  output [15:0] DMAddress,
  output [15:0] DMData,
  output [15:0] WriteBack,
  output [3:0] Flags,
  output [15:0] AluA,
  output [15:0] AluB,
  output [15:0] ALUResult,
  output [3:0] ALUFlags
);

  wire CLKin, FlagEnable, JMP, MemFlag, MOVSignal, multiplexer_6_out, NOPSignal, not_1_out, WE3;
  wire [2:0] A1, A2, RegOut;
  wire [3:0] ALUOp;
  wire [15:0] ExtendedImmediate, multiplexer_2_out, multiplexer_3_out, NonALUOpA, NonALUOpB, NonJumpA,
       NonJumpB, PCPlus1, RD1, RD2;

  Multiplexer multiplexer_1 (.in0(CLK), .in1(1'b0), .out(CLKin), .sel(Halt));
  FetchUnit fetchunit_1 (
    .JMP(JMP), .Clk(CLKin), .Reset(Reset), .WBBus(ALUResult), .IMAddress(IMAddress), .PCPlus1(PCPlus1));
  Decode decode_1 (
    .IMDataIn(IMDataIn), .NZCVIn(Flags), .WE3Out(WE3), .OutAddress(ExtendedImmediate),
    .FlagUpdate(FlagEnable), .Ri1(A1), .MOVSignal(MOVSignal), .Ri2(A2), .Rd(RegOut), .ALUOp(ALUOp),
    .NOPSignal(NOPSignal), .HALTSignal(Halt), .JMP(JMP), .ModifyMemory(MemFlag));
  Multiplexer #(.width(16)) multiplexer_2 (.in0(ALUResult), .in1(WriteBack), .out(multiplexer_2_out), .sel(MemFlag));
  Multiplexer #(.width(16)) multiplexer_3 (.in0(IMAddress), .in1(PCPlus1), .out(multiplexer_3_out), .sel(NOPSignal));
  Multiplexer #(.width(16)) multiplexer_4 (.in0(NonJumpA), .in1(PCPlus1), .out(AluA), .sel(JMP));
  Multiplexer #(.width(16)) multiplexer_5 (.in0(NonJumpB), .in1(ExtendedImmediate), .out(AluB), .sel(JMP));
  ALU alu_1 (.A(AluA), .B(AluB), .ALUOp(ALUOp), .Result(ALUResult), .FlagsNZCV(ALUFlags));
  RegisterFile8x16 registerfile8x16_1 (
    .CLK(CLKin), .WD3(multiplexer_2_out), .A1(A1), .A2(A2), .A3(RegOut), .RESET(Reset), .WE3(WE3),
    .R7(multiplexer_3_out), .RD1(RD1), .RD2(RD2), .RD3(DMData));
  Multiplexer multiplexer_6 (.in0(1'b0), .in1(CLKin), .out(multiplexer_6_out), .sel(MemFlag));
  Multiplexer #(.select(4), .width(16)) multiplexer_7 (
    .in4({16{1'b0}}), .in5({16{1'b0}}), .in8(RD1), .in12(RD1), .out(NonALUOpA), .sel(IMDataIn[12:9]));  // open: in0, in1, in2, in3, in6, in7, in9, in10, in11, in13, in14, in15
  not not_1 (not_1_out, WE3);
  Multiplexer #(.select(4), .width(16)) multiplexer_8 (
    .in4(RD1), .in5(ExtendedImmediate), .in8(RD2), .in12(RD2), .out(NonALUOpB), .sel(IMDataIn[12:9]));  // open: in0, in1, in2, in3, in6, in7, in9, in10, in11, in13, in14, in15
  Multiplexer #(.select(3), .width(16)) multiplexer_9 (
    .in0(NonALUOpA), .in1(RD1), .in2(RD1), .in3(RD1), .in4({16{1'b0}}), .in5({16{1'b0}}), .in6({16{1'b0}}),
    .in7({16{1'b0}}), .out(NonJumpA), .sel(IMDataIn[15:13]));
  Multiplexer #(.select(3), .width(16)) multiplexer_10 (
    .in0(NonALUOpB), .in1(RD2), .in2(RD2), .in3(RD2), .in4(ExtendedImmediate), .in5(ExtendedImmediate),
    .in6(ExtendedImmediate), .in7(ExtendedImmediate), .out(NonJumpB), .sel(IMDataIn[15:13]));
  DataMemory datamemory_1 (
    .DMAddress(ALUResult), .WE(not_1_out), .CLK(multiplexer_6_out), .DMDataIn(DMData), .DMDataOut(WriteBack));
  Register #(.width(4)) FlagRegister (.D(ALUFlags), .en(FlagEnable), .clk(CLKin), .Q(Flags), .clr(Reset));

  assign DMAddress = ALUResult;
  assign IMData = IMDataIn;

  // Other names for the same wires on the sheet: A[15:0] = AluA; B[15:0] = AluB; DataIn[15:0] = DMData;
  //   NonALUSigMOV[3:0] = IMDataIn[12:9]; DecSelect[2:0] = IMDataIn[15:13]; Result[15:0] = ALUResult

  // Notes on the sheet:
  //   Build your CPU here
  //   000 is a Non_ALU Op and 001 is an ALU Op
  //   DecSelect looks at the first 3 bits(15-13), and decides what operation's output is necessary.
  //   Anything of the form 1xx is Mov Immediate
  //   Checks bits 11-9 of NON-ALU Signal to see what must be passed based on what operation.
endmodule

module FrontPanelController (
  input  Clk,
  input  Run,
  input  Step,
  input  Reset,
  input  Halt,
  output CpuClk,
  output RunHalt
);

  wire and_1_out, or_1_out, pull_resistor_1_node, t_ff_1_q;

  T_Flip_Flop t_ff_1 (.T(pull_resistor_1_node), .clk(Run), .Q(t_ff_1_q), .reset(Reset));  // open: Qn, preset
  Pull_Resistor #(.pull(1)) pull_resistor_1 (.node(pull_resistor_1_node));
  or or_1 (or_1_out, t_ff_1_q, Step);
  and and_1 (and_1_out, Clk, t_ff_1_q);
  and and_2 (RunHalt, or_1_out, ~Halt);  // AND_Gate
  Multiplexer multiplexer_1 (.in0(Step), .in1(and_1_out), .out(CpuClk), .sel(t_ff_1_q));
endmodule

module FetchUnit (
  input  JMP,
  input  Clk,
  input  Reset,
  input  [15:0] WBBus,
  output [15:0] IMAddress,
  output [15:0] PCPlus1
);

  wire [15:0] multiplexer_1_out;

  Multiplexer #(.width(16)) multiplexer_1 (.in0(PCPlus1), .in1(WBBus), .out(multiplexer_1_out), .sel(JMP));
  Register #(.width(16)) register_1 (.D(multiplexer_1_out), .clk(Clk), .Q(IMAddress), .clr(Reset));  // open: en
  Adder #(.width(16)) adder_1 (.a(IMAddress), .b(16'h1), .out(PCPlus1));  // open: cin, cout
endmodule

module ALU (
  input  [15:0] A,
  input  [15:0] B,
  input  [3:0] ALUOp,
  output [15:0] Result,
  output [3:0] FlagsNZCV
);

  wire Add_CV, Sub_CV, Z;
  wire [15:0] adder_1_out, and_1_out, divider_1_out, divider_2_rem, multiplier_1_out, multiplier_2_cout,
       not_1_out, or_1_out, shifter_1_out, shifter_2_out, shifter_3_out, shifter_4_out, shifter_5_out,
       subtractor_1_out, xor_1_out;

  Adder #(.width(16)) adder_1 (.a(A), .b(B), .out(adder_1_out), .cout(Add_CV));  // open: cin
  Subtractor #(.width(16)) subtractor_1 (.a(A), .b(B), .out(subtractor_1_out), .bout(Sub_CV));  // open: bin
  Multiplier #(.width(16)) multiplier_1 (.a(A), .b(B), .out(multiplier_1_out));  // open: cin, cout
  Multiplier #(.width(16)) multiplier_2 (.a(A), .b(B), .cout(multiplier_2_cout));  // open: out, cin
  Divider #(.width(16)) divider_1 (.a(A), .b(B), .out(divider_1_out));  // open: upper, rem
  Divider #(.width(16)) divider_2 (.a(A), .b(B), .rem(divider_2_rem));  // open: out, upper
  assign and_1_out = A & B;  // AND_Gate and_1, 16 bits wide
  assign or_1_out = A | B;  // OR_Gate or_1, 16 bits wide
  assign xor_1_out = A ^ B;  // XOR_Gate xor_1, 16 bits wide
  assign not_1_out = ~A;  // NOT_Gate not_1, 16 bits wide
  Shifter #(.width(16)) shifter_1 (.in(A), .\dist (B[3:0]), .out(shifter_1_out));
  Shifter #(.shift("lr"), .width(16)) shifter_2 (.in(A), .\dist (B[3:0]), .out(shifter_2_out));
  Shifter #(.shift("ar"), .width(16)) shifter_3 (.in(A), .\dist (B[3:0]), .out(shifter_3_out));
  Shifter #(.shift("rl"), .width(16)) shifter_4 (.in(A), .\dist (B[3:0]), .out(shifter_4_out));
  Shifter #(.shift("rr"), .width(16)) shifter_5 (.in(A), .\dist (B[3:0]), .out(shifter_5_out));
  Multiplexer #(.select(4), .width(16)) multiplexer_1 (
    .in0(adder_1_out), .in1(subtractor_1_out), .in2(multiplier_1_out), .in3(multiplier_2_cout),
    .in4(divider_1_out), .in5(divider_2_rem), .in6(and_1_out), .in7(or_1_out), .in8(xor_1_out),
    .in9(not_1_out), .in10(shifter_1_out), .in11(shifter_2_out), .in12(shifter_3_out), .in13(shifter_4_out),
    .in14(shifter_5_out), .in15({16{1'b0}}), .out(Result), .sel(ALUOp));
  Multiplexer #(.select(4), .width(4)) multiplexer_2 (
    .in0({Result[15], Z, {2{Add_CV}}}), .in1({Result[15], Z, {2{Sub_CV}}}), .in2({Result[15], Z, 2'b00}),
    .in3({Result[15], Z, 2'b00}), .in4({Result[15], Z, 2'b00}), .in5({Result[15], Z, 2'b00}),
    .in6({Result[15], Z, 2'b00}), .in7({Result[15], Z, 2'b00}), .in8({Result[15], Z, 2'b00}),
    .in9({Result[15], Z, 2'b00}), .in10({Result[15], Z, 2'b00}), .in11({Result[15], Z, 2'b00}),
    .in12({Result[15], Z, 2'b00}), .in13({Result[15], Z, 2'b00}), .in14({Result[15], Z, 2'b00}),
    .in15({Result[15], Z, 2'b00}), .out(FlagsNZCV), .sel(ALUOp));
  nor nor_1 (Z, Result[15], Result[14], Result[13], Result[12], Result[11], Result[10], Result[9], Result[8], Result[7], Result[6], Result[5], Result[4], Result[3], Result[2], Result[1], Result[0]);

  // Other names for the same wires on the sheet: OpCode[3:0] = ALUOp; RES[15:0] = Result; N = Result[15]
endmodule

module RegisterFile8x16 (
  input  CLK,
  input  [15:0] WD3,
  input  [2:0] A1,
  input  [2:0] A2,
  input  [2:0] A3,
  input  RESET,
  input  WE3,
  input  [15:0] R7,
  output [15:0] RD1,
  output [15:0] RD2,
  output [15:0] RD3
);

  wire demultiplexer_2_out7, WER0, WER1, WER2, WER3, WER4, WER5, WER6;
  wire [15:0] ARR7_q, demultiplexer_1_out7, I0, I1, I2, I3, I4, I5, I6, R0_q, R1_q, R2_q, R3_q, R4_q, R5_q,
       R6_q;

  Demultiplexer #(.select(3), .width(16)) demultiplexer_1 (
    .out0(I0), .out1(I1), .out2(I2), .out3(I3), .out4(I4), .out5(I5), .out6(I6), .out7(demultiplexer_1_out7),
    .in(WD3), .sel(A3));
  Demultiplexer #(.select(3)) demultiplexer_2 (
    .out0(WER0), .out1(WER1), .out2(WER2), .out3(WER3), .out4(WER4), .out5(WER5), .out6(WER6),
    .out7(demultiplexer_2_out7), .in(WE3), .sel(A3));
  Register #(.width(16)) R0 (.D(I0), .en(WER0), .clk(CLK), .Q(R0_q), .clr(RESET));
  Register #(.width(16)) R1 (.D(I1), .en(WER1), .clk(CLK), .Q(R1_q), .clr(RESET));
  Register #(.width(16)) R2 (.D(I2), .en(WER2), .clk(CLK), .Q(R2_q), .clr(RESET));
  Register #(.width(16)) R3 (.D(I3), .en(WER3), .clk(CLK), .Q(R3_q), .clr(RESET));
  Register #(.width(16)) R4 (.D(I4), .en(WER4), .clk(CLK), .Q(R4_q), .clr(RESET));
  Register #(.width(16)) R5 (.D(I5), .en(WER5), .clk(CLK), .Q(R5_q), .clr(RESET));
  Register #(.width(16)) R6 (.D(I6), .en(WER6), .clk(CLK), .Q(R6_q), .clr(RESET));
  Register #(.width(16)) ARR7 (.D(R7), .clk(CLK), .Q(ARR7_q), .clr(RESET));  // open: en
  Multiplexer #(.select(3), .width(16)) multiplexer_1 (
    .in0(R0_q), .in1(R1_q), .in2(R2_q), .in3(R3_q), .in4(R4_q), .in5(R5_q), .in6(R6_q), .in7(ARR7_q),
    .out(RD1), .sel(A1));
  Multiplexer #(.select(3), .width(16)) multiplexer_2 (
    .in0(R0_q), .in1(R1_q), .in2(R2_q), .in3(R3_q), .in4(R4_q), .in5(R5_q), .in6(R6_q), .in7(ARR7_q),
    .out(RD2), .sel(A2));
  Multiplexer #(.select(3), .width(16)) multiplexer_3 (
    .in0(R0_q), .in1(R1_q), .in2(R2_q), .in3(R3_q), .in4(R4_q), .in5(R5_q), .in6(R6_q), .in7(ARR7_q),
    .out(RD3), .sel(A3));
endmodule

module Decode (
  input  [15:0] IMDataIn,
  input  [3:0] NZCVIn,
  output WE3Out,
  output [15:0] OutAddress,
  output FlagUpdate,
  output [2:0] Ri1,
  output MOVSignal,
  output [2:0] Ri2,
  output [2:0] Rd,
  output [3:0] ALUOp,
  output NOPSignal,
  output HALTSignal,
  output JMP,
  output ModifyMemory
);

  wire BeqJMP, BJMP, BneJMP, demultiplexer_2_out0, demultiplexer_3_out6, demultiplexer_3_out7, not_1_out,
       WE3NonALU;
  wire [15:0] ALUIn, BopIn, BOpOutAdd, demultiplexer_1_out0, demultiplexer_6_out0, FlagExtended, MOVIn,
       MOVOutAdd, NonALUIn;

  Demultiplexer #(.width(16)) demultiplexer_1 (
    .out0(demultiplexer_1_out0), .out1(MOVIn), .in(IMDataIn), .sel(IMDataIn[15]));
  Demultiplexer #(.select(3)) demultiplexer_2 (
    .out0(demultiplexer_2_out0), .in(1'b1), .sel(IMDataIn[15:13]));  // open: out1, out2, out3, out4, out5, out6, out7
  Demultiplexer #(.select(4)) demultiplexer_3 (
    .out4(BJMP), .out6(demultiplexer_3_out6), .out7(demultiplexer_3_out7), .in(1'b1), .sel(IMDataIn[15:12]));  // open: out0, out1, out2, out3, out5, out8, out9, out10, out11, out12, out13, out14, out15
  Demultiplexer #(.select(4)) demultiplexer_4 (
    .out0(NOPSignal), .out3(HALTSignal), .in(demultiplexer_2_out0), .sel(IMDataIn[12:9]));  // open: out1, out2, out4, out5, out6, out7, out8, out9, out10, out11, out12, out13, out14, out15
  not not_1 (not_1_out, NZCVIn[2]);
  Demultiplexer #(.select(4)) demultiplexer_5 (
    .out1(ModifyMemory), .in(1'b1), .sel(IMDataIn[15:12]));  // open: out0, out2, out3, out4, out5, out6, out7, out8, out9, out10, out11, out12, out13, out14, out15
  Demultiplexer #(.width(16)) demultiplexer_6 (
    .out0(demultiplexer_6_out0), .out1(BopIn), .in(demultiplexer_1_out0), .sel(IMDataIn[14]));
  and BEQ (BeqJMP, demultiplexer_3_out6, NZCVIn[2]);
  and BNE (BneJMP, demultiplexer_3_out7, not_1_out);
  SIgnExtender signextender_1 (.Inn(MOVIn[11:0]), .ExtendedOutput(MOVOutAdd));
  Demultiplexer #(.width(16)) demultiplexer_7 (
    .out0(NonALUIn), .out1({ALUIn[15:13], ALUOp, ALUIn[8:0]}), .in(demultiplexer_6_out0), .sel(IMDataIn[13]));
  Multiplexer #(.select(3)) multiplexer_1 (
    .in0(WE3NonALU), .in1(1'b1), .in2(1'b0), .in3(1'b0), .in4(1'b1), .in5(1'b1), .in6(1'b1), .in7(1'b1),
    .out(WE3Out), .sel(IMDataIn[15:13]));
  Multiplexer #(.select(4)) multiplexer_2 (
    .in0(1'b0), .in3(1'b0), .in4(1'b1), .in5(1'b1), .in8(1'b1), .in12(1'b0), .out(WE3NonALU),
    .sel(IMDataIn[12:9]));  // open: in1, in2, in6, in7, in9, in10, in11, in13, in14, in15
  Multiplexer #(.select(4)) multiplexer_3 (
    .in0(1'b0), .in1(1'b0), .in2(1'b0), .in3(1'b0), .in4(BJMP), .in5(1'b0), .in6(BeqJMP), .in7(BneJMP),
    .in8(1'b0), .in9(1'b0), .in10(1'b0), .in11(1'b0), .in12(1'b0), .in13(1'b0), .in14(1'b0), .in15(1'b0),
    .out(JMP), .sel(IMDataIn[15:12]));
  Multiplexer #(.select(3), .width(3)) multiplexer_4 (
    .in0(NonALUIn[5:3]), .in1(ALUIn[5:3]), .in4(MOVIn[14:12]), .in5(MOVIn[14:12]), .in6(MOVIn[14:12]),
    .in7(MOVIn[14:12]), .out(Rd), .sel(IMDataIn[15:13]));  // open: in2, in3
  SignExtender4bit signextender4bit_1 (.inn(NZCVIn), .Extended(FlagExtended));
  Multiplexer #(.select(3), .width(16)) multiplexer_5 (
    .in0(FlagExtended), .in1({16{1'b0}}), .in2(BOpOutAdd), .in3(BOpOutAdd), .in4(MOVOutAdd), .in5(MOVOutAdd),
    .in6(MOVOutAdd), .in7(MOVOutAdd), .out(OutAddress), .sel(IMDataIn[15:13]));
  Multiplexer #(.select(3), .width(3)) multiplexer_6 (
    .in0(NonALUIn[8:6]), .in1(ALUIn[8:6]), .out(Ri1), .sel(IMDataIn[15:13]));  // open: in2, in3, in4, in5, in6, in7
  SIgnExtender signextender_2 (.Inn(BopIn[11:0]), .ExtendedOutput(BOpOutAdd));
  Multiplexer #(.select(3), .width(3)) multiplexer_7 (
    .in0(NonALUIn[2:0]), .in1(ALUIn[2:0]), .out(Ri2), .sel(IMDataIn[15:13]));  // open: in2, in3, in4, in5, in6, in7
  Multiplexer #(.select(3)) multiplexer_8 (
    .in0(1'b0), .in1(1'b1), .in2(1'b0), .in3(1'b0), .in4(1'b0), .in5(1'b0), .in6(1'b0), .in7(1'b0),
    .out(FlagUpdate), .sel(IMDataIn[15:13]));

  assign MOVSignal = IMDataIn[15];

  // Other names for the same wires on the sheet: Ri2_ALU[2:0] = ALUIn[2:0]; Rd_ALU[2:0] = ALUIn[5:3];
  //   Ri1_ALU[2:0] = ALUIn[8:6]; ALUIn[12:9] = ALUOp; Rd_MOV[2:0] = MOVIn[14:12]; Ri2_NonALU[2:0] = NonALUIn[2:0];
  //   Rd_NonALU[2:0] = NonALUIn[5:3]; Ri1_NoALU[2:0] = NonALUIn[8:6]; ZFlag = NZCVIn[2]

  // Notes on the sheet:
  //   Checks first bit to see if mov
  //   MOV
  //   ALU
  //   Checks 2nd bit to see if Bop or not
  //   NOP and Halt
  //   Figuring out whether we're jumping or not
  //   Checks 3rd bit to see if ALU op
  //   So I use a mux with first 3 bits of IMData as select to choose what my final output Rd will be.
  //   This MUX chooses what the R3 will be
  //   Based on first 3 bits of IMData, we figure out what operation is being run. 
  //   B lm
  //   FlagUpdate?
endmodule

module SIgnExtender (
  input  [11:0] Inn,
  output [15:0] ExtendedOutput
);

  Multiplexer #(.width(5)) multiplexer_1 (.in0({5{1'b0}}), .in1({5{1'b1}}), .out(ExtendedOutput[15:11]), .sel(Inn[11]));

  assign ExtendedOutput[10:0] = Inn[10:0];
endmodule

module DataMemory (
  input  [15:0] DMAddress,
  input  WE,
  input  CLK,
  input  [15:0] DMDataIn,
  output [15:0] DMDataOut
);

  wire comparator_1_eq, comparator_1_gt, not_1_out, ReserveFlag;
  wire [15:0] multiplexer_1_out, subtractor_1_out;

  Subtractor #(.width(16)) subtractor_1 (.a(DMAddress), .b(16'hf230), .out(subtractor_1_out));  // open: bin, bout
  Comparator #(.mode("unsigned"), .width(16)) comparator_1 (
    .a(DMAddress), .b(16'hf230), .gt(comparator_1_gt), .eq(comparator_1_eq));  // open: lt
  Multiplexer #(.width(16)) multiplexer_1 (
    .in0(DMAddress), .in1(subtractor_1_out), .out(multiplexer_1_out), .sel(ReserveFlag));
  or or_1 (ReserveFlag, comparator_1_gt, comparator_1_eq);
  RAM #(.addrWidth(16), .asyncread("true"), .dataWidth(16)) ram_1 (
    .addr(multiplexer_1_out), .we(WE), .oe(not_1_out), .clk(CLK), .din(DMDataIn), .dout(DMDataOut));
  not not_1 (not_1_out, WE);
endmodule

module SignExtender4bit (
  input  [3:0] inn,
  output [15:0] Extended
);

  Multiplexer #(.width(13)) multiplexer_1 (.in0({13{1'b0}}), .in1({13{1'b1}}), .out(Extended[15:3]), .sel(inn[3]));

  assign Extended[2:0] = inn[2:0];
endmodule

module DecimalDisplayControl (
  input  [15:0] DataIn,
  output [3:0] D0,
  output [3:0] D1,
  output [3:0] D2,
  output [3:0] D3,
  output [3:0] D4,
  output Sign
);

  wire [15:0] divider_1_out, divider_2_out, divider_3_out, divider_4_out;
  wire [15:4] divider_1_rem, divider_2_rem, divider_3_rem, divider_4_rem, divider_5_rem;

  Divider #(.width(16)) divider_1 (
    .a(DataIn), .b(16'ha), .out(divider_1_out), .rem({divider_1_rem, D0}));  // open: upper
  Divider #(.width(16)) divider_2 (
    .a(divider_1_out), .b(16'ha), .out(divider_2_out), .rem({divider_2_rem, D1}));  // open: upper
  Divider #(.width(16)) divider_3 (
    .a(divider_2_out), .b(16'ha), .out(divider_3_out), .rem({divider_3_rem, D2}));  // open: upper
  Divider #(.width(16)) divider_4 (
    .a(divider_3_out), .b(16'ha), .out(divider_4_out), .rem({divider_4_rem, D3}));  // open: upper
  Divider #(.width(16)) divider_5 (.a(divider_4_out), .b(16'ha), .rem({divider_5_rem, D4}));  // open: out, upper

  assign Sign = DataIn[15];
endmodule

module DecimalIO (
  input  [15:0] DMData,
  input  [15:0] DMAddress,
  input  CLK,
  input  RESET,
  output [15:0] Data
);

  wire comparator_1_eq;

  Comparator #(.mode("unsigned"), .width(16)) comparator_1 (
    .a(DMAddress), .b({16{1'b1}}), .eq(comparator_1_eq));  // open: gt, lt
  Register #(.width(16)) register_1 (.D(DMData), .en(comparator_1_eq), .clk(CLK), .Q(Data), .clr(RESET));
endmodule
